# Fritzing sketch CandleCircuit (saved by Fritzing 0.9.2b)

parts:
  LED3 = ws2812b [package="smd 2812b"]
  U1 = ESP8266 WiFi Module [part_number=ESP8266]
  U4 = attiny85 [package=dip]
  LED2 = ws2812b [package="smd 2812b"]
  LED1 = ws2812b [package="smd 2812b"]

nets:
  5V: LED3.VDD, LED2.VDD, LED1.VDD
  GND: LED3.VSS, U1.GND, U4.Pin_4, LED2.VSS, LED1.VSS
  N1: LED3.DIN, LED2.DOUT
  3.3V: U1.VCC, U4.Pin_8
  N2: U1.TXD, U4.Pin_2
  N3: U4.Pin_7, LED1.DIN
  N4: LED2.DIN, LED1.DOUT

custom parts:
  ESP8266 WiFi Module: Generic WiFi Module based on the ESP8266 with onboard PCB antenna and UART communications
